# Fritzing sketch esquema_final (saved by Fritzing 1.0.1rc)
breadboards: 1

parts:
  920KV_Motor1 = DJI 920 KV Motor
  920KV_Motor2 = DJI 920 KV Motor
  920KV_Motor3 = DJI 920 KV Motor
  920KV_Motor4 = DJI 920 KV Motor
  ESC1 = ESC 30A
  ESC2 = ESC 30A
  ESC3 = ESC 30A
  ESC4 = ESC 30A
  S1 = Toggle Switch [package=THT]
  Raspberry_Pi1 = Raspberry Pi Zero
  IC1 = Rasberry Pi NIOR Camera [chip_label=IC package="DIP (Dual Inline) [THT]"]  # not connected
  U1 = SUP500F [package=sup500f]
  M1 = Dagu DGServo 9g (Top view) [part_number=RS001B]
  U2 = LIPO-11.1V-3 Cells [package=Li-Po-2200]
  Componente1 = Arduino Pro
  J1 = Piezo Speaker

nets:
  N1: 920KV_Motor1.w, ESC1.C
  N2: 920KV_Motor1.v, ESC1.B
  N3: 920KV_Motor1.u, ESC1.A
  N4: 920KV_Motor2.w, ESC2.C
  N5: 920KV_Motor2.v, ESC2.B
  N6: 920KV_Motor2.u, ESC2.A
  N7: 920KV_Motor3.w, ESC3.C
  N8: 920KV_Motor3.v, ESC3.B
  N9: 920KV_Motor3.u, ESC3.A
  N10: 920KV_Motor4.w, ESC4.C
  N11: 920KV_Motor4.v, ESC4.B
  N12: 920KV_Motor4.u, ESC4.A
  VCC: ESC1.v+, ESC2.v+, ESC3.v+, ESC4.v+, Raspberry_Pi1.5V, U1.VCC, M1.vcc, Componente1.VCC
  GND: ESC1.GND#4, ESC2.GND#4, ESC3.GND#4, ESC4.GND#4, Raspberry_Pi1.GND, U1.GND, M1.gnd, Componente1.GND, J1.pin1
  N13: ESC1.In, Componente1.A0
  N14: ESC2.In, Componente1.A1
  N15: ESC3.In, Componente1.A2
  N16: ESC4.In, Componente1.A3
  N17: S1.L1, U2.+
  N18: Raspberry_Pi1.GIPO23, J1.pin2
  N19: Raspberry_Pi1.GIPO18, M1.pulse
  N20: Raspberry_Pi1.GIPO15, Componente1.RX
  N21: Raspberry_Pi1.GIPO14, Componente1.TX
  N22: U1.RX-I, Componente1.D0/RX
  N23: U1.TX-O, Componente1.D1/TX

notes:
  m1m2 m3 m4
  7,4 v
  Li-Po
  2 Cells

custom parts:
  DJI 920 KV Motor: DJI Brushless Outrunner 2212/920K Motor F330-550
  ESC 30A: Electronic Speed Controller - 30A
  Raspberry Pi Zero: The Raspberry Pi Zero is the latest single board computer to be released by the Raspberry Pi Foundation. It is the entry level model Raspberry Pi perfect for hobbyists, makers and industrial engineers looking to create solutions where small size and low power consumption are important. This is especially relevant for applications in the wearables space as well as up and coming applications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
  Rasberry Pi NIOR Camera: Camera
  LIPO-11.1V-3 Cells: Li-Po Battery-11.1V-3Cells-2200mAh
